// Digital circuit ALU_Control.dig as structural Verilog
module ALU_Control (
  input  AO_1,
  input  AO_0,
  input  [5:0] F,
  output [3:0] AC
);

  wire and_1_out, or_1_out;

  or or_1 (or_1_out, F[3], F[0]);
  and and_1 (and_1_out, AO_1, F[1]);
  and and_2 (AC[0], AO_1, or_1_out);
  or or_2 (AC[2], AO_0, and_1_out);
  or or_3 (AC[1], ~AO_1, ~F[2]);  // Or
  // Pins of 5 and 6 bits meet at F
  // Pins of 1 and 4 bits meet at {1'b0, AC[2:0]}

  assign AC[3] = 1'b0;

  // Notes on the sheet:
  //   AO_1: ALUOp_1
  //   AO_0: ALUOp_0
  //   AC: ALUControl
endmodule
