// Digital circuit equal_and_not_zero.dig as structural Verilog
module equal_and_not_zero (
  input  [4:0] A,
  input  [4:0] B,
  output eq
);

  wire comparator_1_eq, comparator_2_eq, not_1_out;

  Comparator #(.Bits(5)) comparator_1 (.a(A), .b(B), .eq(comparator_1_eq));  // open: gt, lt
  Comparator #(.Bits(5)) comparator_2 (.a({5{1'b0}}), .b(B), .eq(comparator_2_eq));  // open: gt, lt
  not not_1 (not_1_out, comparator_2_eq);
  and and_1 (eq, comparator_1_eq, not_1_out);

  // Notes on the sheet:
  //   eq: B == A and B != 0
endmodule
