// Digital circuit forwarding-unit.dig as structural Verilog
module forwarding_unit (
  input  [4:0] RS,
  input  [4:0] RT,
  input  [4:0] EX_MEM_dest,
  input  [4:0] MEM_WB_dest,
  input  EX_MEM_rw,
  input  MEM_WB_rw,
  output [1:0] FA,
  output [1:0] FB
);

  wire equal_and_not_zero_1_eq, equal_and_not_zero_2_eq, equal_and_not_zero_3_eq, equal_and_not_zero_4_eq;

  equal_and_not_zero equal_and_not_zero_1 (.A(RS), .B(EX_MEM_dest), .eq(equal_and_not_zero_1_eq));
  and and_1 (FA[1], equal_and_not_zero_1_eq, EX_MEM_rw);
  equal_and_not_zero equal_and_not_zero_2 (.A(RS), .B(MEM_WB_dest), .eq(equal_and_not_zero_2_eq));
  and and_2 (FA[0], equal_and_not_zero_2_eq, MEM_WB_rw);
  equal_and_not_zero equal_and_not_zero_3 (.A(RT), .B(EX_MEM_dest), .eq(equal_and_not_zero_3_eq));
  and and_3 (FB[1], equal_and_not_zero_3_eq, EX_MEM_rw);
  equal_and_not_zero equal_and_not_zero_4 (.A(RT), .B(MEM_WB_dest), .eq(equal_and_not_zero_4_eq));
  and and_4 (FB[0], equal_and_not_zero_4_eq, EX_MEM_rw);
endmodule
