// Digital circuit instruction_mem.dig as structural Verilog
module instruction_mem (
  input  [31:0] _32b__ADDR,
  input  _1b__Enable,
  output [31:0] _32b__Out
);

  wire [31:0] div_1_q;

  Div #(.Bits(32)) div_1 (.a(_32b__ADDR), .b(32'h4), .q(div_1_q));  // open: r
  ROM #(.AddrBits(8), .Bits(32)) rom_1 (.A(div_1_q[7:0]), .sel(_1b__Enable), .D(_32b__Out));

  // Notes on the sheet:
  //   contents of rom_1 (hex, n*v repeats v):
  //   0,0,22100005,0,0,0,210f820,0,0,0,23ff0005,0,0,0,23ff0005,0,0,0
  //   ,23ff0005,0,0,0,23ff0005,0,0,0,23ff0005
endmodule
