// Digital circuit memory_24x32.dig as structural Verilog
module memory_24x32 (
  input  [23:0] address,
  input  [31:0] write_data,
  input  mem_write,
  input  Clk,
  input  mem_read,
  input  in_7,
  input  [23:0] a,
  output [31:0] data
);

  wire or_1_out;
  wire [23:0] div_1_q, multiplexer_1_out;
  wire [31:0] ramdualport_1_d;

  or or_1 (or_1_out, mem_read, in_7);
  Multiplexer #(.Bits(24)) multiplexer_1 (.sel(in_7), .in_0(address), .in_1(a), .out(multiplexer_1_out));
  Div #(.Bits(24)) div_1 (.a(multiplexer_1_out), .b(24'h4), .q(div_1_q));  // open: r
  RAMDualPort #(.AddrBits(24), .Bits(32)) ramdualport_1 (
    .A(div_1_q), .Din(write_data), .str(mem_write), .C(Clk), .ld(or_1_out), .D(ramdualport_1_d));
  Multiplexer #(.Bits(32)) multiplexer_2 (.sel(or_1_out), .in_0({32{1'b0}}), .in_1(ramdualport_1_d), .out(data));

  // Notes on the sheet:
  //   address: Endereço a ser acessado
  //   write_data: Dados a serem gravados
  //   mem_write: Mem Write
  //   Clk: Clock
  //   mem_read: Mem Read
endmodule
