// Digital circuit PC.dig as structural Verilog
module PC (
  input  Clok,
  input  [31:0] PC_IN,
  output [31:0] PC_OUT
);

  wire not_1_out, or_1_out;
  wire [31:0] d_ff_as_1_q;

  D_FF_AS #(.Bits(32)) d_ff_as_1 (.Set(1'b0), .D(PC_IN), .C(~Clok), .Clr(not_1_out), .Q(d_ff_as_1_q));  // open: nQ
  or or_1 (or_1_out, Clok, or_1_out);
  D_FF_AS #(.Bits(32)) d_ff_as_2 (.Set(1'b0), .D(d_ff_as_1_q), .C(Clok), .Clr(not_1_out), .Q(PC_OUT));  // open: nQ
  not not_1 (not_1_out, or_1_out);
endmodule
