// Digital circuit EX-MEM.dig as structural Verilog
module EX_MEM (
  input  [31:0] R_2,
  input  [31:0] Result,
  input  [4:0] Dest,
  input  Clk,
  input  MTR,
  input  MW,
  input  MR,
  input  RW,
  output [31:0] O_R2,
  output [31:0] O_Result,
  output [4:0] O_Dest,
  output O_MTR,
  output O_MW,
  output O_MR,
  output O_RW
);

  wire d_ff_1_q, d_ff_2_q, d_ff_3_q, d_ff_4_q;
  wire [4:0] d_ff_7_q;
  wire [31:0] d_ff_5_q, d_ff_6_q;

  D_FF d_ff_1 (.D(RW), .C(~Clk), .Q(d_ff_1_q));  // open: nQ
  D_FF d_ff_2 (.D(MR), .C(~Clk), .Q(d_ff_2_q));  // open: nQ
  D_FF d_ff_3 (.D(MW), .C(~Clk), .Q(d_ff_3_q));  // open: nQ
  D_FF d_ff_4 (.D(MTR), .C(~Clk), .Q(d_ff_4_q));  // open: nQ
  D_FF #(.Bits(32)) d_ff_5 (.D(Result), .C(~Clk), .Q(d_ff_5_q));  // open: nQ
  D_FF #(.Bits(32)) d_ff_6 (.D(R_2), .C(~Clk), .Q(d_ff_6_q));  // open: nQ
  D_FF #(.Bits(5)) d_ff_7 (.D(Dest), .C(~Clk), .Q(d_ff_7_q));  // open: nQ
  D_FF d_ff_8 (.D(d_ff_1_q), .C(Clk), .Q(O_RW));  // open: nQ
  D_FF d_ff_9 (.D(d_ff_2_q), .C(Clk), .Q(O_MR));  // open: nQ
  D_FF d_ff_10 (.D(d_ff_3_q), .C(Clk), .Q(O_MW));  // open: nQ
  D_FF d_ff_11 (.D(d_ff_4_q), .C(Clk), .Q(O_MTR));  // open: nQ
  D_FF #(.Bits(32)) d_ff_12 (.D(d_ff_5_q), .C(Clk), .Q(O_Result));  // open: nQ
  D_FF #(.Bits(32)) d_ff_13 (.D(d_ff_6_q), .C(Clk), .Q(O_R2));  // open: nQ
  D_FF #(.Bits(5)) d_ff_14 (.D(d_ff_7_q), .C(Clk), .Q(O_Dest));  // open: nQ

  // Notes on the sheet:
  //   R_2: Dado lido do registrador 2
  //   O_R2: Dado lido do registrador 2
  //   Result: Dado lido do registrador 1
  //   O_Result: Dado lido do registrador 1
  //   Dest: Sinal extendido
  //   O_Dest: Sinal extendido
  //   M
endmodule
