// Digital circuit EX-MEM_PC.dig as structural Verilog
module EX_MEM_PC (
  input  Clk,
  input  [31:0] PC,
  input  Alu_zero,
  input  APC,
  output [31:0] O_PC,
  output O_zero,
  output O_APC
);

  wire pulse_1_p;

  pulse pulse_1 (.Clk(Clk), .P(pulse_1_p));
  // reg32 reg32_1: pin names not known; wires that end beside it: PC, Clk, pulse_1_p, O_PC
  // reg reg_1: pin names not known; wires that end beside it: Alu_zero, Clk, pulse_1_p, O_zero
  // reg reg_2: pin names not known; wires that end beside it: APC, Clk, pulse_1_p, O_APC
endmodule
