// Digital circuit ID-EX.dig as structural Verilog
module ID_EX (
  input  [31:0] ID_rtData,
  input  [31:0] ID_rsData,
  input  [31:0] ID_const,
  input  ID_memToReg,
  input  clock,
  input  [4:0] ID_rsAddr,
  input  [4:0] ID_rtAddr,
  input  [4:0] ID_rdAddr,
  input  [5:0] ID_funct,
  input  [1:0] ID_aluOp,
  input  ID_regDst,
  input  ID_aluSrc,
  input  ID_memRead,
  input  ID_memWrite,
  input  ID_regwrite,
  input  ID_branch,
  output [31:0] EX_rtData,
  output [31:0] EX_rsData,
  output [31:0] EX_const,
  output MEM_memToReg,
  output [4:0] EX_rsAddr,
  output [4:0] EX_rtAddr,
  output [4:0] EX_rdAddr,
  output [5:0] EX_funct,
  output [1:0] EX_aluOP,
  output EX_regDst,
  output EX_aluSrc,
  output MEM_memRead,
  output MEM_memWrite,
  output WB_regwrite,
  output EXE_branch
);

  wire pulse_1_p;

  pulse pulse_1 (.Clk(clock), .P(pulse_1_p));
  // reg reg_1: pin names not known; wires that end beside it: ID_regwrite, clock, pulse_1_p, WB_regwrite
  // reg reg_2: pin names not known; wires that end beside it: ID_memToReg, clock, pulse_1_p, MEM_memToReg
  // reg reg_3: pin names not known; wires that end beside it: ID_memRead, clock, pulse_1_p, MEM_memRead
  // reg reg_4: pin names not known; wires that end beside it: ID_memWrite, clock, pulse_1_p, MEM_memWrite
  // reg reg_5: pin names not known; wires that end beside it: ID_branch, clock, pulse_1_p, EXE_branch
  // reg reg_6: pin names not known; wires that end beside it: ID_regDst, clock, pulse_1_p, EX_regDst
  // reg reg_7: pin names not known; wires that end beside it: ID_aluSrc, clock, pulse_1_p, EX_aluSrc
  reg2 reg2_1 (.In(ID_aluOp), .Clk(clock), .Clr(pulse_1_p), .Out(EX_aluOP));
  reg32 reg32_1 (.In(ID_rsData), .Clk(clock), .Clr(pulse_1_p), .Out(EX_rsData));
  reg32 reg32_2 (.In(ID_rtData), .Clk(clock), .Clr(pulse_1_p), .Out(EX_rtData));
  reg32 reg32_3 (.In(ID_const), .Clk(clock), .Clr(pulse_1_p), .Out(EX_const));
  reg5 reg5_1 (.In(ID_rsAddr), .Clk(clock), .Clr(pulse_1_p), .Out(EX_rsAddr));
  reg5 reg5_2 (.In(ID_rtAddr), .Clk(clock), .Clr(pulse_1_p), .Out(EX_rtAddr));
  reg5 reg5_3 (.In(ID_rdAddr), .Clk(clock), .Clr(pulse_1_p), .Out(EX_rdAddr));
  reg6 reg6_1 (.In(ID_funct), .Clk(clock), .Clr(pulse_1_p), .Out(EX_funct));

  // Notes on the sheet:
  //   ID_rtData: Dado lido do registrador 2
  //   EX_rtData: Dado lido do registrador 2
  //   ID_rsData: Dado lido do registrador 1
  //   EX_rsData: Dado lido do registrador 1
  //   ID_const: Sinal extendido
  //   EX_const: Sinal extendido
  //   ID_rsAddr: Dado lido do registrador 2
  //   EX_rsAddr: Dado lido do registrador 2
  //   ID_rtAddr: Sinal extendido
  //   EX_rtAddr: Sinal extendido
  //   ID_rdAddr: Sinal extendido
  //   EX_rdAddr: Sinal extendido
endmodule
