// Digital circuit ID-EX_PC.dig as structural Verilog
module ID_EX_PC (
  input  Clk,
  input  [31:0] PC,
  input  APC,
  output [31:0] O_PC,
  output O_APC
);

  wire pulse_1_p;

  pulse pulse_1 (.Clk(Clk), .P(pulse_1_p));
  // reg32 reg32_1: pin names not known; wires that end beside it: PC, Clk, pulse_1_p, O_PC
  // reg reg_1: pin names not known; wires that end beside it: APC, Clk, pulse_1_p, O_APC
endmodule
