// Digital circuit ID-EX_part_2.dig as structural Verilog
module ID_EX_part_2 (
  input  Clk,
  input  [4:0] RS,
  input  [4:0] RT,
  input  [4:0] RD,
  input  [5:0] Funct,
  output [4:0] O_RS,
  output [4:0] O_RT,
  output [4:0] O_RD,
  output [5:0] O_Funct
);

  wire pulse_1_p;

  pulse pulse_1 (.Clk(Clk), .P(pulse_1_p));
  reg5 reg5_1 (.In(RS), .Clk(Clk), .Clr(pulse_1_p), .Out(O_RS));
  reg5 reg5_2 (.In(RT), .Clk(Clk), .Clr(pulse_1_p), .Out(O_RT));
  reg5 reg5_3 (.In(RD), .Clk(Clk), .Clr(pulse_1_p), .Out(O_RD));
  reg6 reg6_1 (.In(Funct), .Clk(Clk), .Clr(pulse_1_p), .Out(O_Funct));

  // Notes on the sheet:
  //   RS: Dado lido do registrador 2
  //   O_RS: Dado lido do registrador 2
  //   RT: Sinal extendido
  //   O_RT: Sinal extendido
  //   RD: Sinal extendido
  //   O_RD: Sinal extendido
endmodule
