// Digital circuit IF-ID.dig as structural Verilog
module IF_ID (
  input  [31:0] In,
  input  Clk,
  output [31:0] Out
);

  wire [31:0] d_ff_1_q;

  D_FF #(.Bits(32)) d_ff_1 (.D(In), .C(~Clk), .Q(d_ff_1_q));  // open: nQ
  D_FF #(.Bits(32)) d_ff_2 (.D(d_ff_1_q), .C(Clk), .Q(Out));  // open: nQ

  // Notes on the sheet:
  //   In: (32 bits) Instrução
  //   Out: (32 bits) Instrução
endmodule
