// Digital circuit MEM-WB.dig as structural Verilog
module MEM_WB (
  input  [31:0] Alu_res,
  input  [31:0] Read_D,
  input  [4:0] Dest,
  input  Clk,
  input  MTR,
  input  RW,
  output [31:0] O_Alu_res,
  output [31:0] O_Read_D,
  output [4:0] O_Dest,
  output O_MTR,
  output O_RW
);

  wire d_ff_1_q, d_ff_2_q;
  wire [4:0] d_ff_5_q;
  wire [31:0] d_ff_3_q, d_ff_4_q;

  D_FF d_ff_1 (.D(RW), .C(~Clk), .Q(d_ff_1_q));  // open: nQ
  D_FF d_ff_2 (.D(MTR), .C(~Clk), .Q(d_ff_2_q));  // open: nQ
  D_FF #(.Bits(32)) d_ff_3 (.D(Read_D), .C(~Clk), .Q(d_ff_3_q));  // open: nQ
  D_FF #(.Bits(32)) d_ff_4 (.D(Alu_res), .C(~Clk), .Q(d_ff_4_q));  // open: nQ
  D_FF #(.Bits(5)) d_ff_5 (.D(Dest), .C(~Clk), .Q(d_ff_5_q));  // open: nQ
  D_FF d_ff_6 (.D(d_ff_1_q), .C(Clk), .Q(O_RW));  // open: nQ
  D_FF d_ff_7 (.D(d_ff_2_q), .C(Clk), .Q(O_MTR));  // open: nQ
  D_FF #(.Bits(32)) d_ff_8 (.D(d_ff_3_q), .C(Clk), .Q(O_Read_D));  // open: nQ
  D_FF #(.Bits(32)) d_ff_9 (.D(d_ff_4_q), .C(Clk), .Q(O_Alu_res));  // open: nQ
  D_FF #(.Bits(5)) d_ff_10 (.D(d_ff_5_q), .C(Clk), .Q(O_Dest));  // open: nQ

  // Notes on the sheet:
  //   Alu_res: Dado lido do registrador 2
  //   O_Alu_res: Dado lido do registrador 2
  //   Read_D: Dado lido da memória
  //   O_Read_D: Dado lido do registrador 1
  //   Dest: Sinal extendido
  //   O_Dest: Sinal extendido
endmodule
