// Digital circuit PC_ppl.dig as structural Verilog
module PC_ppl (
  input  Clk,
  input  [31:0] PC,
  output [31:0] O_PC
);

  wire pulse_1_p;

  pulse pulse_1 (.Clk(Clk), .P(pulse_1_p));
  reg32 reg32_1 (.In(PC), .Clk(Clk), .Clr(pulse_1_p), .Out(O_PC));
endmodule
