// Digital circuit reg.dig as structural Verilog
module \reg  (
  input  [31:0] In,
  input  Clk,
  output [31:0] Out
);

  wire not_1_out, or_1_out;
  wire [31:0] d_ff_as_1_q;

  D_FF_AS #(.Bits(32)) d_ff_as_1 (.Set(1'b0), .D(In), .C(~Clk), .Clr(not_1_out), .Q(d_ff_as_1_q));  // open: nQ
  or or_1 (or_1_out, Clk, or_1_out);
  D_FF_AS #(.Bits(32)) d_ff_as_2 (.Set(1'b0), .D(d_ff_as_1_q), .C(Clk), .Clr(not_1_out), .Q(Out));  // open: nQ
  not not_1 (not_1_out, or_1_out);

  // Notes on the sheet:
  //   In: (32 bits) Instrução
  //   Out: (32 bits) Instrução
endmodule
