// Digital circuit reg32.dig as structural Verilog
module reg32 (
  input  [31:0] In,
  input  Clk,
  input  Clr,
  output [31:0] Out
);

  wire [31:0] d_ff_as_1_q;

  D_FF_AS #(.Bits(32)) d_ff_as_1 (.Set(1'b0), .D(In), .C(~Clk), .Clr(Clr), .Q(d_ff_as_1_q));  // open: nQ
  D_FF_AS #(.Bits(32)) d_ff_as_2 (.Set(1'b0), .D(d_ff_as_1_q), .C(Clk), .Clr(Clr), .Q(Out));  // open: nQ

  // Notes on the sheet:
  //   In: (32 bits) Instrução
  //   Out: (32 bits) Instrução
endmodule
