// Digital circuit 32FFD.dig as structural Verilog
module _32FFD (
  input  [32:0] D_0,
  input  [32:0] D_1,
  input  [32:0] D_2,
  input  [32:0] D_3,
  input  [32:0] D_4,
  input  [32:0] D_5,
  input  [32:0] D_6,
  input  [32:0] D_7,
  input  [32:0] D_8,
  input  [32:0] D_9,
  input  [32:0] D_10,
  input  [32:0] D_11,
  input  [32:0] D_12,
  input  [32:0] D_13,
  input  [32:0] D_14,
  input  [32:0] D_15,
  input  [32:0] D_16,
  input  [32:0] D_17,
  input  [32:0] D_18,
  input  [32:0] D_19,
  input  [32:0] D_20,
  input  [32:0] D_21,
  input  [32:0] D_22,
  input  [32:0] D_23,
  input  [32:0] D_24,
  input  [32:0] D_25,
  input  [32:0] D_26,
  input  [32:0] D_27,
  input  [32:0] D_28,
  input  [32:0] D_29,
  input  [32:0] D_30,
  input  [32:0] D_31,
  output [31:0] Q_0,
  output [31:0] Q_1,
  output [31:0] Q_2,
  output [31:0] Q_3,
  output [31:0] Q_4,
  output [31:0] Q_5,
  output [31:0] Q_6,
  output [31:0] Q_7,
  output [31:0] Q_8,
  output [31:0] Q_9,
  output [31:0] Q_10,
  output [31:0] Q_11,
  output [31:0] Q_12,
  output [31:0] Q_13,
  output [31:0] Q_14,
  output [31:0] Q_15,
  output [31:0] Q_16,
  output [31:0] Q_17,
  output [31:0] Q_18,
  output [31:0] Q_19,
  output [31:0] Q_20,
  output [31:0] Q_21,
  output [31:0] Q_22,
  output [31:0] Q_23,
  output [31:0] Q_24,
  output [31:0] Q_25,
  output [31:0] Q_26,
  output [31:0] Q_27,
  output [31:0] Q_28,
  output [31:0] Q_29,
  output [31:0] Q_30,
  output [31:0] Q_31
);

  D_FF #(.Bits(32)) d_ff_1 (.D(D_0[31:0]), .C(D_0[32]), .Q(Q_0));  // open: nQ
  D_FF #(.Bits(32)) d_ff_2 (.D(D_1[31:0]), .C(D_1[32]), .Q(Q_1));  // open: nQ
  D_FF #(.Bits(32)) d_ff_3 (.D(D_2[31:0]), .C(D_2[32]), .Q(Q_2));  // open: nQ
  D_FF #(.Bits(32)) d_ff_4 (.D(D_3[31:0]), .C(D_3[32]), .Q(Q_3));  // open: nQ
  D_FF #(.Bits(32)) d_ff_5 (.D(D_4[31:0]), .C(D_4[32]), .Q(Q_4));  // open: nQ
  D_FF #(.Bits(32)) d_ff_6 (.D(D_5[31:0]), .C(D_5[32]), .Q(Q_5));  // open: nQ
  D_FF #(.Bits(32)) d_ff_7 (.D(D_6[31:0]), .C(D_6[32]), .Q(Q_6));  // open: nQ
  D_FF #(.Bits(32)) d_ff_8 (.D(D_7[31:0]), .C(D_7[32]), .Q(Q_7));  // open: nQ
  D_FF #(.Bits(32)) d_ff_9 (.D(D_8[31:0]), .C(D_8[32]), .Q(Q_8));  // open: nQ
  D_FF #(.Bits(32)) d_ff_10 (.D(D_9[31:0]), .C(D_9[32]), .Q(Q_9));  // open: nQ
  D_FF #(.Bits(32)) d_ff_11 (.D(D_10[31:0]), .C(D_10[32]), .Q(Q_10));  // open: nQ
  D_FF #(.Bits(32)) d_ff_12 (.D(D_11[31:0]), .C(D_11[32]), .Q(Q_11));  // open: nQ
  D_FF #(.Bits(32)) d_ff_13 (.D(D_12[31:0]), .C(D_12[32]), .Q(Q_12));  // open: nQ
  D_FF #(.Bits(32)) d_ff_14 (.D(D_13[31:0]), .C(D_13[32]), .Q(Q_13));  // open: nQ
  D_FF #(.Bits(32)) d_ff_15 (.D(D_14[31:0]), .C(D_14[32]), .Q(Q_14));  // open: nQ
  D_FF #(.Bits(32)) d_ff_16 (.D(D_15[31:0]), .C(D_15[32]), .Q(Q_15));  // open: nQ
  D_FF #(.Bits(32)) d_ff_17 (.D(D_16[31:0]), .C(D_16[32]), .Q(Q_16));  // open: nQ
  D_FF #(.Bits(32)) d_ff_18 (.D(D_17[31:0]), .C(D_17[32]), .Q(Q_17));  // open: nQ
  D_FF #(.Bits(32)) d_ff_19 (.D(D_18[31:0]), .C(D_18[32]), .Q(Q_18));  // open: nQ
  D_FF #(.Bits(32)) d_ff_20 (.D(D_19[31:0]), .C(D_19[32]), .Q(Q_19));  // open: nQ
  D_FF #(.Bits(32)) d_ff_21 (.D(D_20[31:0]), .C(D_20[32]), .Q(Q_20));  // open: nQ
  D_FF #(.Bits(32)) d_ff_22 (.D(D_21[31:0]), .C(D_21[32]), .Q(Q_21));  // open: nQ
  D_FF #(.Bits(32)) d_ff_23 (.D(D_22[31:0]), .C(D_22[32]), .Q(Q_22));  // open: nQ
  D_FF #(.Bits(32)) d_ff_24 (.D(D_23[31:0]), .C(D_23[32]), .Q(Q_23));  // open: nQ
  D_FF #(.Bits(32)) d_ff_25 (.D(D_24[31:0]), .C(D_24[32]), .Q(Q_24));  // open: nQ
  D_FF #(.Bits(32)) d_ff_26 (.D(D_25[31:0]), .C(D_25[32]), .Q(Q_25));  // open: nQ
  D_FF #(.Bits(32)) d_ff_27 (.D(D_26[31:0]), .C(D_26[32]), .Q(Q_26));  // open: nQ
  D_FF #(.Bits(32)) d_ff_28 (.D(D_27[31:0]), .C(D_27[32]), .Q(Q_27));  // open: nQ
  D_FF #(.Bits(32)) d_ff_29 (.D(D_28[31:0]), .C(D_28[32]), .Q(Q_28));  // open: nQ
  D_FF #(.Bits(32)) d_ff_30 (.D(D_29[31:0]), .C(D_29[32]), .Q(Q_29));  // open: nQ
  D_FF #(.Bits(32)) d_ff_31 (.D(D_30[31:0]), .C(D_30[32]), .Q(Q_30));  // open: nQ
  D_FF #(.Bits(32)) d_ff_32 (.D(D_31[31:0]), .C(D_31[32]), .Q(Q_31));  // open: nQ
endmodule
