// Digital circuit 32x32.dig as structural Verilog
module _32x32 (
  input  [31:0] write_data,
  input  [4:0] rd_addr,
  input  reg_write,
  input  [4:0] rs_addr,
  input  [4:0] rt_addr,
  input  clock,
  output [31:0] rs_data,
  output [31:0] rt_data,
  output [31:0] R31
);

  wire clock_t;
  wire [31:0] A_0, A_1, A_2, A_3, A_4, A_5, A_6, A_7, A_8, A_9, A_10, A_11, A_12, A_13, A_14, A_15, A_16,
       A_17, A_18, A_19, A_20, A_21, A_22, A_23, A_24, A_25, A_26, A_27, A_28, A_29, A_30, multiplexer_1_out,
       multiplexer_3_out;
  wire [32:0] demultiplexer_1_out_0, demultiplexer_1_out_1, demultiplexer_1_out_2, demultiplexer_1_out_3,
       demultiplexer_1_out_4, demultiplexer_1_out_5, demultiplexer_1_out_6, demultiplexer_1_out_7,
       demultiplexer_1_out_8, demultiplexer_1_out_9, demultiplexer_1_out_10, demultiplexer_1_out_11,
       demultiplexer_1_out_12, demultiplexer_1_out_13, demultiplexer_1_out_14, demultiplexer_1_out_15,
       demultiplexer_1_out_16, demultiplexer_1_out_17, demultiplexer_1_out_18, demultiplexer_1_out_19,
       demultiplexer_1_out_20, demultiplexer_1_out_21, demultiplexer_1_out_22, demultiplexer_1_out_23,
       demultiplexer_1_out_24, demultiplexer_1_out_25, demultiplexer_1_out_26, demultiplexer_1_out_27,
       demultiplexer_1_out_28, demultiplexer_1_out_29, demultiplexer_1_out_30, demultiplexer_1_out_31;

  Delay #(.delayTime(4)) delay_1 (.in(clock), .out(clock_t));
  Demultiplexer #(.Selector_Bits(5), .Bits(33)) demultiplexer_1 (
    .sel(rd_addr), .in({reg_write, write_data}), .out_0(demultiplexer_1_out_0),
    .out_1(demultiplexer_1_out_1), .out_2(demultiplexer_1_out_2), .out_3(demultiplexer_1_out_3),
    .out_4(demultiplexer_1_out_4), .out_5(demultiplexer_1_out_5), .out_6(demultiplexer_1_out_6),
    .out_7(demultiplexer_1_out_7), .out_8(demultiplexer_1_out_8), .out_9(demultiplexer_1_out_9),
    .out_10(demultiplexer_1_out_10), .out_11(demultiplexer_1_out_11), .out_12(demultiplexer_1_out_12),
    .out_13(demultiplexer_1_out_13), .out_14(demultiplexer_1_out_14), .out_15(demultiplexer_1_out_15),
    .out_16(demultiplexer_1_out_16), .out_17(demultiplexer_1_out_17), .out_18(demultiplexer_1_out_18),
    .out_19(demultiplexer_1_out_19), .out_20(demultiplexer_1_out_20), .out_21(demultiplexer_1_out_21),
    .out_22(demultiplexer_1_out_22), .out_23(demultiplexer_1_out_23), .out_24(demultiplexer_1_out_24),
    .out_25(demultiplexer_1_out_25), .out_26(demultiplexer_1_out_26), .out_27(demultiplexer_1_out_27),
    .out_28(demultiplexer_1_out_28), .out_29(demultiplexer_1_out_29), .out_30(demultiplexer_1_out_30),
    .out_31(demultiplexer_1_out_31));
  _32FFD _32ffd_1 (
    .D_0(demultiplexer_1_out_0), .D_1(demultiplexer_1_out_1), .D_2(demultiplexer_1_out_2),
    .D_3(demultiplexer_1_out_3), .D_4(demultiplexer_1_out_4), .D_5(demultiplexer_1_out_5),
    .D_6(demultiplexer_1_out_6), .D_7(demultiplexer_1_out_7), .D_8(demultiplexer_1_out_8),
    .D_9(demultiplexer_1_out_9), .D_10(demultiplexer_1_out_10), .D_11(demultiplexer_1_out_11),
    .D_12(demultiplexer_1_out_12), .D_13(demultiplexer_1_out_13), .D_14(demultiplexer_1_out_14),
    .D_15(demultiplexer_1_out_15), .D_16(demultiplexer_1_out_16), .D_17(demultiplexer_1_out_17),
    .D_18(demultiplexer_1_out_18), .D_19(demultiplexer_1_out_19), .D_20(demultiplexer_1_out_20),
    .D_21(demultiplexer_1_out_21), .D_22(demultiplexer_1_out_22), .D_23(demultiplexer_1_out_23),
    .D_24(demultiplexer_1_out_24), .D_25(demultiplexer_1_out_25), .D_26(demultiplexer_1_out_26),
    .D_27(demultiplexer_1_out_27), .D_28(demultiplexer_1_out_28), .D_29(demultiplexer_1_out_29),
    .D_30(demultiplexer_1_out_30), .D_31(demultiplexer_1_out_31), .Clk(clock_t), .Q_0(A_0), .Q_1(A_1),
    .Q_2(A_2), .Q_3(A_3), .Q_4(A_4), .Q_5(A_5), .Q_6(A_6), .Q_7(A_7), .Q_8(A_8), .Q_9(A_9), .Q_10(A_10),
    .Q_11(A_11), .Q_12(A_12), .Q_13(A_13), .Q_14(A_14), .Q_15(A_15), .Q_16(A_16), .Q_17(A_17), .Q_18(A_18),
    .Q_19(A_19), .Q_20(A_20), .Q_21(A_21), .Q_22(A_22), .Q_23(A_23), .Q_24(A_24), .Q_25(A_25), .Q_26(A_26),
    .Q_27(A_27), .Q_28(A_28), .Q_29(A_29), .Q_30(A_30), .Q_31(R31));
  Multiplexer #(.Selector_Bits(5), .Bits(32)) multiplexer_1 (
    .sel(rs_addr), .in_0(A_0), .in_1(A_1), .in_2(A_2), .in_3(A_3), .in_4(A_4), .in_5(A_5), .in_6(A_6),
    .in_7(A_7), .in_8(A_8), .in_9(A_9), .in_10(A_10), .in_11(A_11), .in_12(A_12), .in_13(A_13), .in_14(A_14),
    .in_15(A_15), .in_16(A_16), .in_17(A_17), .in_18(A_18), .in_19(A_19), .in_20(A_20), .in_21(A_21),
    .in_22(A_22), .in_23(A_23), .in_24(A_24), .in_25(A_25), .in_26(A_26), .in_27(A_27), .in_28(A_28),
    .in_29(A_29), .in_30(A_30), .in_31(R31), .out(multiplexer_1_out));
  Multiplexer #(.Bits(32)) multiplexer_2 (.sel(clock_t), .in_0({32{1'b0}}), .in_1(multiplexer_1_out), .out(rs_data));
  Multiplexer #(.Selector_Bits(5), .Bits(32)) multiplexer_3 (
    .sel(rt_addr), .in_0(A_0), .in_1(A_1), .in_2(A_2), .in_3(A_3), .in_4(A_4), .in_5(A_5), .in_6(A_6),
    .in_7(A_7), .in_8(A_8), .in_9(A_9), .in_10(A_10), .in_11(A_11), .in_12(A_12), .in_13(A_13), .in_14(A_14),
    .in_15(A_15), .in_16(A_16), .in_17(A_17), .in_18(A_18), .in_19(A_19), .in_20(A_20), .in_21(A_21),
    .in_22(A_22), .in_23(A_23), .in_24(A_24), .in_25(A_25), .in_26(A_26), .in_27(A_27), .in_28(A_28),
    .in_29(A_29), .in_30(A_30), .in_31(R31), .out(multiplexer_3_out));
  Multiplexer #(.Bits(32)) multiplexer_4 (.sel(clock_t), .in_0({32{1'b0}}), .in_1(multiplexer_3_out), .out(rt_data));

  // Other names for the same wires on the sheet: A_31[31:0] = R31; get_1[4:0] = rs_addr; get_2[4:0] = rt_addr;
  //   WE = reg_write

  // Notes on the sheet:
  //   write_data: (32 bits) Dado a ser escrito
  //   rd_addr: (5 bits) Endereço a ser escrito
  //   reg_write: (1 bit) Write enable
endmodule
