// Digital circuit FlipFlop_D_force_clear.dig as structural Verilog
module FlipFlop_D_force_clear (
  input  D,
  input  C,
  output Q
);

  wire and_1_out, and_2_out, nor_1_out, not_1_out, or_1_out, or_2_out;

  not not_1 (not_1_out, D);
  and and_1 (and_1_out, D, C);
  and and_2 (and_2_out, C, not_1_out);
  or or_1 (or_1_out, C, or_1_out);
  or or_2 (or_2_out, ~or_1_out, and_2_out);  // Or
  nor nor_1 (nor_1_out, and_1_out, Q);
  nor nor_2 (Q, nor_1_out, or_2_out);
endmodule
