// Digital circuit Stall.dig as structural Verilog
module Stall (
  input  ID_EX_memRead,
  input  [4:0] ID_EX_rt,
  input  [4:0] IF_ID_rs,
  input  [4:0] IF_ID_rt,
  input  branch,
  input  jump,
  output ID_stall,
  output IF_stall
);

  wire and_1_out, comparator_1_eq, comparator_2_eq, or_3_out;

  or or_1 (ID_stall, branch, and_1_out);
  or or_2 (IF_stall, jump, branch);
  and and_1 (and_1_out, ID_EX_memRead, or_3_out);
  or or_3 (or_3_out, comparator_2_eq, comparator_1_eq);
  Comparator #(.Bits(5)) comparator_1 (.a(IF_ID_rs), .b(ID_EX_rt), .eq(comparator_1_eq));  // open: gt, lt
  Comparator #(.Bits(5)) comparator_2 (.a(IF_ID_rt), .b(ID_EX_rt), .eq(comparator_2_eq));  // open: gt, lt
endmodule
