// Digital circuit ula.dig as structural Verilog
module ula (
  input  [3:0] ALUControl,
  input  [31:0] A,
  input  [31:0] B,
  input  [5:0] Shamt,
  output Zero,
  output [31:0] Resultado
);

  wire comparator_1_eq, comparator_1_lt;
  wire [31:0] add_1_s, and_1_out, barrelshifter_1_out, barrelshifter_2_out, barrelshifter_3_out,
       extensao_de_sinal_1_32_1_s, extensao_de_sinal_1_32_2_s, nor_1_out, or_1_out, sub_1_s, xor_1_out;

  assign nor_1_out = ~(A | B);  // NOr nor_1, 32 bits wide
  assign xor_1_out = A ^ B;  // XOr xor_1, 32 bits wide
  BarrelShifter #(.Bits(32), .barrelShifterMode("arithmetic"), .direction("right")) barrelshifter_1 (
    .in(A), .shift(Shamt), .out(barrelshifter_1_out));
  BarrelShifter #(.Bits(32), .direction("right")) barrelshifter_2 (.in(A), .shift(Shamt), .out(barrelshifter_2_out));
  BarrelShifter #(.Bits(32)) barrelshifter_3 (.in(A), .shift(Shamt), .out(barrelshifter_3_out));
  extensao_de_sinal_1_32 extensao_de_sinal_1_32_1 (.A(comparator_1_lt), .S(extensao_de_sinal_1_32_1_s));
  Comparator #(.Bits(32)) comparator_1 (.a(A), .b(B), .eq(comparator_1_eq), .lt(comparator_1_lt));  // open: gt
  extensao_de_sinal_1_32 extensao_de_sinal_1_32_2 (.A(comparator_1_eq), .S(extensao_de_sinal_1_32_2_s));
  Sub #(.Bits(32)) sub_1 (.a(A), .b(B), .c_i(1'b0), .s(sub_1_s));  // open: c_o
  Add #(.Bits(32)) add_1 (.a(A), .b(B), .c_i(1'b0), .s(add_1_s));  // open: c_o
  assign or_1_out = A | B;  // Or or_1, 32 bits wide
  assign and_1_out = A & B;  // And and_1, 32 bits wide
  Multiplexer #(.Selector_Bits(4), .Bits(32)) multiplexer_1 (
    .sel(ALUControl), .in_0(and_1_out), .in_1(or_1_out), .in_2(add_1_s), .in_3({32{1'b0}}),
    .in_4({32{1'b0}}), .in_5({32{1'b0}}), .in_6(sub_1_s), .in_7(extensao_de_sinal_1_32_1_s),
    .in_8(barrelshifter_3_out), .in_9(barrelshifter_2_out), .in_10(barrelshifter_1_out), .in_11({32{1'b0}}),
    .in_12(xor_1_out), .in_13(nor_1_out), .in_14(extensao_de_sinal_1_32_2_s), .in_15({32{1'b0}}),
    .out(Resultado));
  zero zero_1 (.A(Resultado), .Zero(Zero));
endmodule
