// Digital circuit zero.dig as structural Verilog
module zero (
  input  [31:0] A,
  output Zero
);

  wire or_1_out, or_2_out, or_3_out, or_4_out, or_5_out, or_6_out, or_7_out, or_8_out, or_9_out, or_10_out,
       or_11_out, or_12_out, or_13_out, or_14_out, or_15_out, or_16_out, or_17_out, or_18_out, or_19_out,
       or_20_out, or_21_out, or_22_out, or_23_out, or_24_out, or_25_out, or_26_out, or_27_out, or_28_out,
       or_29_out, or_30_out, or_31_out;

  or or_1 (or_1_out, A[0], A[1]);
  or or_2 (or_2_out, or_1_out, A[2]);
  or or_3 (or_3_out, or_2_out, A[3]);
  or or_4 (or_4_out, or_3_out, A[4]);
  or or_5 (or_5_out, or_4_out, A[5]);
  or or_6 (or_6_out, or_5_out, A[6]);
  or or_7 (or_7_out, or_6_out, A[7]);
  or or_8 (or_8_out, or_7_out, A[8]);
  or or_9 (or_9_out, or_8_out, A[9]);
  or or_10 (or_10_out, or_9_out, A[10]);
  or or_11 (or_11_out, or_10_out, A[11]);
  or or_12 (or_12_out, or_11_out, A[12]);
  or or_13 (or_13_out, or_12_out, A[13]);
  or or_14 (or_14_out, or_13_out, A[14]);
  or or_15 (or_15_out, or_14_out, A[15]);
  or or_16 (or_16_out, or_15_out, A[16]);
  or or_17 (or_17_out, or_16_out, A[17]);
  or or_18 (or_18_out, or_17_out, A[18]);
  or or_19 (or_19_out, or_18_out, A[19]);
  or or_20 (or_20_out, or_19_out, A[20]);
  or or_21 (or_21_out, or_20_out, A[21]);
  or or_22 (or_22_out, or_21_out, A[22]);
  or or_23 (or_23_out, or_22_out, A[23]);
  or or_24 (or_24_out, or_23_out, A[24]);
  or or_25 (or_25_out, or_24_out, A[25]);
  or or_26 (or_26_out, or_25_out, A[26]);
  or or_27 (or_27_out, or_26_out, A[27]);
  or or_28 (or_28_out, or_27_out, A[28]);
  or or_29 (or_29_out, or_28_out, A[29]);
  or or_30 (or_30_out, or_29_out, A[30]);
  or or_31 (or_31_out, or_30_out, A[31]);
  not not_1 (Zero, or_31_out);
endmodule
